# Fritzing sketch TeensyHCSR04 (saved by Fritzing 0.7.12b)
breadboards: 1

parts:
  Teensy1 = Teensy 2.0
  Part1 = SRF05 Ultrasonic Rangefinder
  Part2 = 7segment4digitLED

nets:
  GND: Teensy1.GND, Part1.GND, Part2.16
  N1: Teensy1.D7, Part1.Trig
  N2: Teensy1.B4, Part1.Echo
  N3: Teensy1.F0, Part2.9
  VCC: Teensy1.VCC, Part1.VCC, Part2.15
